# Fritzing sketch solar_panel (saved by Fritzing 0.9.2b)
breadboards: 1

parts:
  R1 = Resistor [tolerance=±5% resistance=100k package=THT]
  R2 = Resistor [tolerance=±5% resistance=100k package=THT]
  D1 = SOLAR-IXYS [package=solarbit-12x1]

nets:
  N1: R1.Pin_0, D1.C
  N2: R2.Pin_0, D1.A
